# Fritzing sketch Lesson203 (saved by Fritzing 0.9.2b)
breadboards: 1

parts:
  Breakout1 = BMP280 [package=Breakout]
  Raspberry_Pi1 = Raspberry Pi B+

nets:
  VIN: Breakout1.VIN, Raspberry_Pi1.5V
  GND: Breakout1.GND, Raspberry_Pi1.GND
  N1: Breakout1.SCK, Raspberry_Pi1.GPIO3
  N2: Breakout1.SDI, Raspberry_Pi1.GPIO2

custom parts:
  BMP280: Barometric Pressure and Temperature Sensor
  Raspberry Pi B+: The awesome Raspberry Pi ARM Board with 40 pin gipo. Ready for special designed Raspberry Pi B+ Hat (Hardware attached (on) top)
