# Fritzing sketch Lesson204 (saved by Fritzing 0.9.2b)
breadboards: 1

parts:
  MCP3008 = IC, DIP package, 16 pins [chip_label=MCP3008 part_number=MCP3008]
  Raspberry_Pi1 = Raspberry Pi 2
  R1 = Rotary Potentiometer (Small) [maximum_resistance=10kΩ package=THT]
  R2 = Rotary Potentiometer (Small) [maximum_resistance=10kΩ package=THT]
  R5 = PHOTOCELL [package=photocell-kit]
  R3 = Resistor [tolerance=±5% resistance=560 package="2010 [SMD]"]
  SPKR1 = Loudspeaker  # not connected

nets:
  N1: MCP3008.pin1, R1.wiper
  N2: MCP3008.pin2, R2.wiper
  N3: MCP3008.pin3, R5.P$2, R3.Pin_0
  N4: MCP3008.pin9, Raspberry_Pi1.GND, R1.leg1, R2.leg1, R5.P$1
  N5: MCP3008.pin10, Raspberry_Pi1.GPIO8
  N6: MCP3008.pin11, Raspberry_Pi1.GPIO10
  N7: MCP3008.pin12, Raspberry_Pi1.GPIO9
  N8: MCP3008.pin13, Raspberry_Pi1.GPIO11
  N9: MCP3008.pin14, MCP3008.pin15, MCP3008.pin16, Raspberry_Pi1.3v3, R1.leg2, R2.leg2, R3.Pin_1
