# Fritzing sketch Lesson205 (saved by Fritzing 0.9.2b)
breadboards: 1

parts:
  SENSOR1 = TCS34725 RGB Color Sensor
  Raspberry_Pi2 = Raspberry Pi 2
  S1 = Momentary Switch [package=ksa_sealed_tac_switch]
  R1 = Resistor [tolerance=±5% resistance=10k package=THT]
  SPKR2 = Loudspeaker  # not connected

nets:
  N1: SENSOR1.SDA, Raspberry_Pi2.GPIO2
  GND: SENSOR1.GND, Raspberry_Pi2.GND, S1.2
  VDD: SENSOR1.VDD, Raspberry_Pi2.5V, R1.Pin_1
  N2: Raspberry_Pi2.GPIO4, S1.4, R1.Pin_0

custom parts:
  TCS34725 RGB Color Sensor: TCS34725 RGB Color Sensor with LED
